# Fritzing sketch Motherboard (saved by Fritzing 0.9.3b)
circuit board: 3.56966cm x 1.28272cm
circuit board: 4.6cm x 6.3cm
circuit board: 21cm x 14cm

parts:
  J1 = female pin header, 1 pin [form="♀ (female)"]  # not connected
  J2 = female pin header, 1 pin [form="♀ (female)"]  # not connected
  J3 = female pin header, 1 pin [form="♀ (female)"]  # not connected
  J4 = female pin header, 1 pin [form="♀ (female)"]  # not connected
  J5 = female pin header, 8 pins [form="♀ (female)"]  # not connected
  J6 = female pin header, 8 pins [form="♀ (female)"]  # not connected
  J7 = female pin header, 4 pins [form="♀ (female)"]
  J8 = female pin header, 2 pins [form="♀ (female)"]
  J9 = female pin header, 2 pins [form="♀ (female)"]  # not connected
  J11 = female pin header, 2 pins [form="♀ (female)"]  # not connected
  J12 = female pin header, 2 pins [form="♀ (female)"]  # not connected
  J13 = female pin header, 2 pins [form="♀ (female)"]
  J14 = female pin header, 2 pins [form="♀ (female)"]
  J15 = female pin header, 4 pins [form="♀ (female)"]
  J10 = female pin header, 2 pins [form="♀ (female)"]
  J18 = female pin header, 4 pins [form="♀ (female)"]  # not connected
  J19 = female pin header, 3 pins [form="♀ (female)"]
  J22 = female pin header, 8 pins [form="♀ (female)"]  # not connected
  J23 = female pin header, 8 pins [form="♀ (female)"]  # not connected
  Componente1 = Arduino Mega ADK (Rev3)  # not connected
  J25 = female pin header, 8 pins [form="♀ (female)"]  # not connected
  J24 = female pin header, 4 pins [form="♀ (female)"]  # not connected
  Componente2 = Arduino Mega ADK (Rev3)  # not connected
  J26 = double row female pin header, 6 pins [form="♀ (female)"]  # not connected
  J28 = female pin header, 10 pins [form="♀ (female)"]  # not connected
  J29 = female pin header, 8 pins [form="♀ (female)"]  # not connected
  J30 = female pin header, 18 pins [form="♀ (female)"]  # not connected
  J31 = female pin header, 18 pins [form="♀ (female)"]  # not connected
  J32 = female pin header, 4 pins [form="♀ (female)"]  # not connected
  J33 = female pin header, 1 pin [form="♀ (female)"]  # not connected
  J34 = female pin header, 1 pin [form="♀ (female)"]  # not connected
  U4 = TLP621 [package=THT]
  Q4 = NPN-Transistor [package="TO92 [THT]"]
  J35 = female pin header, 2 pins [form="♀ (female)"]
  R6 = Resistor [tolerance=±5% resistance=220 package=THT]
  R9 = Resistor [tolerance=±5% resistance=220 package=THT]
  J36 = female pin header, 1 pin [form="♀ (female)"]  # not connected
  J37 = female pin header, 1 pin [form="♀ (female)"]  # not connected
  J38 = female pin header, 1 pin [form="♀ (female)"]  # not connected
  J39 = female pin header, 2 pins [form="♀ (female)"]
  J40 = female pin header, 4 pins [form="♀ (female)"]  # not connected
  J17 = female pin header, 1 pin [form="♀ (female)"]  # not connected
  J16 = female pin header, 1 pin [form="♀ (female)"]  # not connected
  R22 = Resistor [tolerance=±5% resistance=220 package=THT]
  J62 = female pin header, 2 pins [form="♀ (female)"]

nets:
  N1: J7.pin1, J15.pin1, J10.pin2, J39.pin1
  N2: J7.pin4, J15.pin4, J10.pin1, J39.pin2
  N3: J8.pin1, J14.pin2
  N4: J8.pin2, J13.pin2
  N5: J19.pin2, J19.pin3
  N6: U4.Pin_1, R9.Pin_1
  N7: U4.Pin_4, J35.pin2
  N8: U4.Pin_3, R6.Pin_0
  N9: Q4.B, R6.Pin_1
  N10: Q4.C, J35.pin1
  N11: R22.Pin_1, J62.pin2

notes:
  GND
  3V3
  Vin
  Clk
  MISO
  MOSI
  CS
  VBEN
  IRQ
  Relé Module
  SD
  DCDC
  Step
  Down
  CREATED BY FEDERICO BOLELLI
  5V
  IN2
  5V_ext
  IN3
  SG1
  5v
  SG2
  A0
  A1
  A2
  A3
  A5
  A4
  A6
  A8
  A9
  A15
  A12
  A10
  A11
  A14
  7
  6
  1
  3
  16
  17
  5
  14
  4
  2
  0
  15
  IN1
  12V in
  12 Vin
  5V in
  The Available Pins
  Are Labeled
  (remember to remove the
  copper for all the other)
  7V out
  DFPlayer
  OUT+
  OUT-
  IN+
  IN-
  OPT
  220 Ω
  Segnale Arduino
  GND Arduino
  +5v EXT
  -5v EXT
  RX
  TX
  SPK_1
  SPK_2
  SD in
  LED
  Amplificatore
  10 KΩ
  5V Arduino
  SIG Arduino
  220 KΩ
